# Fritzing sketch smart-door-lock-circuit-diagram_revised (saved by Fritzing 1.0.5)
breadboards: 1

parts:
  SG1 = Buzzer 12mm [part_number=COM-07950 package=buzzer-12mm-ns]
  DHT11_1 = DHT11 module
  Part2 = 4x4 Keypad [part_number=101207]
  Part3 = RFID-RC522 [part_number=101218]
  SERVO1 = Tower Pro SG90 servo [part_number=101246]
  LCD2004-I2C1 = LCD2004-I2C
  U1 = LuaNode32 / ESP32 [part_number=ESP32S-PIN30]

nets:
  N1: SG1.1, U1.RX2
  VCC: SG1.2, DHT11_1.VCC, SERVO1.+5V, LCD2004-I2C1.VCC
  GND: DHT11_1.GND, Part3.GND, SERVO1.GND, LCD2004-I2C1.GND
  N2: DHT11_1.DATA, U1.TX2
  N3: Part2.1, U1.D13
  N4: Part2.2, U1.D12
  N5: Part2.3, U1.D14
  N6: Part2.4, U1.D27
  N7: Part2.5, U1.D26
  N8: Part2.6, U1.D25
  N9: Part2.7, U1.D33
  N10: Part2.8, U1.D32
  N11: Part3.SDA, U1.D5
  N12: Part3.SCK, U1.D18
  N13: Part3.MOSI, U1.D23
  N14: Part3.MISO, U1.D19
  N15: Part3.RST, U1.D4
  3.3V: Part3.3.3V, U1.3V3
  N16: SERVO1.Signal, U1.D2
  N17: LCD2004-I2C1.SDA, U1.D21
  N18: LCD2004-I2C1.SCL, U1.D22

custom parts:
  Buzzer 12mm: Buzzer 12mm Spark Fun Electronics SKU : Comp-Buzzer Through hole This is a small 12mm round speaker that operates around the audible 2kHz range. You can use these speakers to create simple music or user interfaces. This is not a true piezoelectric speaker but behaves similarly. Instead of a piezoelectric crystal that vibrates with an electric current, this tiny speaker uses an electromagnet to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
  DHT11 module: https://cdn-learn.adafruit.com/downloads/pdf/dht.pdf DHT11 black pcb module reference by:https://github.com/adafruit/Fritzing-Library/blob/master/parts/DHT11%20Humitidy%20and%20Temperature%20Sensor.fzpz
  4x4 Keypad: Matrix membrane keypad 4x4
  Tower Pro SG90 servo: Original file by John De Cristofaro http://www.adafruit.com/products/1449 Adafruit Feedback Servo (Small) Edited by: e-radionica.com 28/9/2015
  LCD2004-I2C: A standard character display with 4x20 characters. Comes in many colors with LCM2004 IIC attached.
  LuaNode32 / ESP32: New Image for LuaNode32 DOIT ESP32 DEVKIT V1. Base parts from LuaNode32 / ESP32 ESP32 based LuaNode32 by G.Noorlander DOIT Esp32 DevKit v1 (30 pins long, 11 pins width) by Werner Rothschopf (modified by vanepp Dec 2018)
